# Fritzing sketch Sketch-DataGuard-01 (saved by Fritzing 0.9.3b)

parts:
  RHT1 = Humidity and Temperature Sensor RHT03
  U1 = NodeMCU V3.0

nets:
  VCC: RHT1.Vcc, U1.3V3
  N1: RHT1.Data-signal, U1.D5
  N2: RHT1.GND_2, U1.GND

notes:
  ← DHT22
  ↓ NodeMCU ESP8266

custom parts:
  NodeMCU V3.0: ESP8266 based NodeMCU
